# Fritzing sketch Semaforo_lua (saved by Fritzing 0.9.3b)
breadboards: 1

parts:
  Raspberry_Pi_1 = Raspberry Pi 3 [part_number=RPI-3-V1.2]
  J1 = Basic Servo
  R1 = Resistor [tolerance=±5% resistance=1 package="2010 [SMD]"]
  R2 = Resistor [tolerance=±5% resistance=1 package="2010 [SMD]"]
  LED1 = smd LED [color="Red (633nm)" package="1206 [SMD]"]
  LED2 = smd LED [color="Green (555nm)" package="1206 [SMD]"]

nets:
  GND: Raspberry_Pi_1.GND, J1.gnd, R1.Pin_0, R2.Pin_0
  N1: Raspberry_Pi_1.GIPO15, LED2.cathode
  N2: Raspberry_Pi_1.GIPO14, LED1.cathode
  5V: Raspberry_Pi_1.5V, J1.vcc
  N3: R1.Pin_1, LED1.anode
  N4: R2.Pin_1, LED2.anode
